// Logisim project rak47.circ as structural Verilog: 1 circuit, main circuit main
module main (
  input  A,
  input  B,
  input  C,
  input  D,
  output ny,
  output KNF_X,
  output zadanie_x,
  output DNF_x,
  output DNF_y,
  output KNF_y
);

  wire and_1_out, and_2_out, and_3_out, and_4_out, and_5_out, and_6_out, and_7_out, and_8_out, not_1_out,
       not_2_out, not_3_out, not_4_out, not_5_out, not_6_out, not_7_out, not_8_out, not_9_out, or_1_out,
       or_2_out, or_3_out, or_4_out, or_5_out, or_6_out, or_7_out, xnor_1_out, xor_1_out;

  not not_1 (not_1_out, D);
  not not_2 (not_2_out, A);
  not not_3 (not_3_out, B);
  not not_4 (not_4_out, C);
  not not_5 (not_5_out, D);
  xnor xnor_1 (xnor_1_out, A, B);
  xor xor_1 (xor_1_out, C, not_1_out);
  and and_1 (and_1_out, B, D);
  not not_6 (not_6_out, A);
  not not_7 (not_7_out, B);
  not not_8 (not_8_out, C);
  not not_9 (not_9_out, D);
  and and_2 (and_2_out, B, not_2_out);
  and and_3 (and_3_out, not_3_out, A);
  and and_4 (and_4_out, not_4_out, D);
  and and_5 (and_5_out, C, not_5_out);
  and and_6 (and_6_out, B, C, D);
  and and_7 (and_7_out, not_3_out, C, not_5_out);
  and and_8 (and_8_out, not_3_out, not_4_out, D);
  or or_1 (or_1_out, not_6_out, not_7_out, not_8_out, not_9_out);
  or or_2 (or_2_out, not_6_out, not_7_out, C, D);
  or or_3 (or_3_out, not_9_out, not_8_out, A, B);
  or or_4 (or_4_out, A, B, C, D);
  or or_5 (or_5_out, B, not_8_out, not_9_out);
  or or_6 (or_6_out, not_7_out, C);
  or or_7 (or_7_out, C, D);
  nand nand_1 (zadanie_x, xnor_1_out, xor_1_out);
  xnor xnor_2 (ny, xor_1_out, and_1_out);
  and and_9 (KNF_X, or_1_out, or_2_out, or_3_out, or_4_out);
  or or_8 (DNF_x, and_2_out, and_3_out, and_4_out, and_5_out);
  or or_9 (DNF_y, and_5_out, and_6_out, and_7_out, and_8_out);
  and and_10 (KNF_y, or_5_out, or_6_out, or_7_out);

  // Notes on the sheet:
  //   DNF
  //   KNF
  //      KNF y
endmodule
